# Fritzing sketch DP H01 ATMEGA VERSION (saved by Fritzing 0.9.3b)
circuit board: 10cm x 10cm
breadboards: 1

parts:
  ATMEGA_328 = atmega328 [package=dip]
  DRIVER1 = L293D [package=THT]
  DRIVER2 = L293D [package=THT]
  ESP = ESP8266 WiFi Module [part_number=ESP8266]
  RELAY3 = OMRON PCB Power Relay – G5LE [part_number="G5LE-1\n" package=THT]
  RELAY1 = OMRON PCB Power Relay – G5LE [part_number="G5LE-1\n" package=THT]
  RELAY2 = OMRON PCB Power Relay – G5LE [part_number="G5LE-1\n" package=THT]
  OUT4 = screw terminal, 3 pins
  OUT6 = screw terminal, 3 pins
  OUT6_2 = screw terminal, 3 pins
  OUT5 = screw terminal, 3 pins
  OUT8 = screw terminal, 3 pins
  OUT9 = screw terminal, 3 pins
  RELAY4 = OMRON PCB Power Relay – G5LE [part_number="G5LE-1\n" package=THT]
  RELAY5 = OMRON PCB Power Relay – G5LE [part_number="G5LE-1\n" package=THT]
  RELAY6 = OMRON PCB Power Relay – G5LE [part_number="G5LE-1\n" package=THT]
  IN3 = screw terminal, 2 pins
  IN4 = screw terminal, 2 pins
  IN5 = screw terminal, 2 pins
  IN6 = screw terminal, 2 pins
  IN7 = screw terminal, 2 pins
  IN8 = screw terminal, 2 pins
  IN9 = screw terminal, 2 pins
  LM319 = Voltage Regulator [package=to220-adj]
  R7 = Resistor [tolerance=±5% resistance=220 package=THT]
  R8 = Resistor [tolerance=±5% resistance=220 package=THT]
  D2 = Rectifier Diode [part_number=1N4001 package="300 mil [THT]"]
  D1 = Rectifier Diode [part_number=1N4001 package="300 mil [THT]"]
  SW3 = Toggle Switch [package=THT]
  FUSE3 = female pin header, 2 pins [form="♀ (female)"]
  Y1 = CRYSTAL [package=hc49us]
  C1 = Capacitor [package=cap-pth-small2]
  C2 = Capacitor [package=cap-pth-small2]
  R9 = Resistor [tolerance=±5% resistance=220 package=THT]
  S2 = Toggle Switch [package=THT]

nets:
  N1: ATMEGA_328.RESET, R9.Pin_1
  N2: ATMEGA_328.D0_(RX), IN4.pin1
  N3: ATMEGA_328.D1_(TX), IN5.pin1
  N4: ATMEGA_328.D2, ESP.TXD
  N5: ATMEGA_328.D3_(PWM), ESP.RXD
  N6: ATMEGA_328.D4, IN6.pin1
  N7: ATMEGA_328.XLAT1, ATMEGA_328.XLAT2, Y1.1, Y1.2, C1.2, C2.2
  N8: ATMEGA_328.D5_(PWM), IN7.pin1
  N9: ATMEGA_328.D6_(PWM), IN8.pin1
  N10: ATMEGA_328.D7, IN3.pin1
  N11: ATMEGA_328.D8, DRIVER2.In_2
  N12: ATMEGA_328.D9_(PWM), DRIVER2.In_3
  N13: ATMEGA_328.D10_(PWM), DRIVER2.In_4
  N14: ATMEGA_328.D11_(PWM), DRIVER2.In_1
  N15: ATMEGA_328.D12, DRIVER1.In_3
  N16: ATMEGA_328.D13, DRIVER1.In_4
  N17: ATMEGA_328.AVCC, DRIVER1.Enable_1, DRIVER1.+V, LM319.IN, D2.cathode, D1.cathode, FUSE3.pin2, R9.Pin_0, S2.L2
  GND: ATMEGA_328.GND, ESP.GND, RELAY3.COIL2, RELAY2.COIL2, RELAY4.COIL2, LM319.ADJ, S2.L1
  N18: ATMEGA_328.A0, S2.COM
  N19: DRIVER1.+Vmotor, DRIVER1.Enable_2, DRIVER2.Enable_1, DRIVER2.+V
  N20: DRIVER1.Out_3_(_Controlled_by_Enable_2_), RELAY3.COIL1
  N21: DRIVER1.Out_4_(_Controlled_by_Enable_2_), RELAY4.COIL1
  N22: DRIVER2.Out_1_(_Controlled_by_Enable_1_), RELAY6.A
  N23: DRIVER2.0V, RELAY1.COIL2
  N24: DRIVER2.Out_2_(_Controlled_by_Enable_1_), RELAY5.A
  N25: DRIVER2.+Vmotor, DRIVER2.Enable_2
  N26: DRIVER2.Out_3_(_Controlled_by_Enable_2_), RELAY1.COIL1
  N27: DRIVER2.Out_4_(_Controlled_by_Enable_2_), RELAY2.COIL1
  N28: ESP.VCC, ESP.CH_PD, LM319.OUT, R8.Pin_1
  N29: RELAY3.A, OUT6_2.pin3
  N30: RELAY3.C, OUT6_2.pin2
  N31: RELAY3.B, OUT6_2.pin1
  N32: RELAY1.A, OUT8.pin3
  N33: RELAY1.C, OUT8.pin2
  N34: RELAY1.B, OUT8.pin1
  N35: RELAY2.A, OUT9.pin3
  N36: RELAY2.C, OUT9.pin2
  N37: RELAY2.B, OUT9.pin1
  N38: OUT4.pin1, RELAY4.B
  N39: OUT4.pin2, RELAY4.C
  N40: OUT4.pin3, RELAY4.A
  N41: OUT6.pin1, RELAY6.COIL1
  N42: OUT6.pin2, RELAY6.C
  N43: OUT6.pin3, RELAY6.COIL2
  N44: OUT5.pin1, RELAY5.COIL1
  N45: OUT5.pin2, RELAY5.C
  N46: OUT5.pin3, RELAY5.COIL2
  N47: RELAY6.B, IN9.pin2, SW3.L1, C1.1, C2.1
  N48: IN3.pin2, IN4.pin2, IN5.pin2, IN6.pin2, IN7.pin2, IN8.pin2
  N49: IN9.pin1, FUSE3.pin1
  N50: R7.Pin_0, D2.anode, D1.anode, SW3.COM, SW3.L2
  N51: R7.Pin_1, R8.Pin_0

notes:
  IN-
  IN+
  +
  -
  A0
  MADE IN EGYPT
  DP COMPANY
  DP S02
  D7
  D6
  D3
  D4
  D2
  D5

custom parts:
  ESP8266 WiFi Module: Generic WiFi Module based on the ESP8266 with onboard PCB antenna and UART communications
