# Fritzing sketch DP H01 TEST 1 (saved by Fritzing 0.9.3b)
circuit board: 10cm x 10cm
breadboards: 1

parts:
  U1 = ESP8266 NodeMCU LoLin module
  IN15 = screw terminal, 2 pins
  OUT11 = screw terminal, 3 pins
  IN19 = screw terminal, 2 pins
  RELAY5 = OMRON PCB Power Relay – G5LE [part_number="G5LE-1\n" package=THT]
  RELAY8 = OMRON PCB Power Relay – G5LE [part_number="G5LE-1\n" package=THT]
  RELAY6 = OMRON PCB Power Relay – G5LE [part_number="G5LE-1\n" package=THT]
  IN20 = screw terminal, 2 pins
  OUT13 = screw terminal, 3 pins
  IN16 = screw terminal, 2 pins
  IN17 = screw terminal, 2 pins
  OUT12 = screw terminal, 3 pins
  IN18 = screw terminal, 2 pins
  OUT10 = screw terminal, 3 pins
  RELAY9 = OMRON PCB Power Relay – G5LE [part_number="G5LE-1\n" package=THT]
  RELAY10 = OMRON PCB Power Relay – G5LE [part_number="G5LE-1\n" package=THT]
  OUT14 = screw terminal, 3 pins
  OUT15 = screw terminal, 3 pins
  RELAY7 = OMRON PCB Power Relay – G5LE [part_number="G5LE-1\n" package=THT]
  IN21 = screw terminal, 2 pins
  D3 = Rectifier Diode [part_number=1N4001 package="300 mil [THT]"]
  D4 = Rectifier Diode [part_number=1N4001 package="300 mil [THT]"]
  SW4 = Toggle Switch [package=THT]
  FUSE4 = female pin header, 2 pins [form="♀ (female)"]

nets:
  N1: U1.D0, RELAY6.COIL2
  N2: U1.D1, RELAY8.COIL2
  N3: U1.D2, RELAY7.COIL2
  N4: U1.D3, RELAY10.COIL1
  N5: U1.D4, RELAY9.COIL1
  N6: U1.GND, IN15.pin1, IN19.pin1, RELAY5.COIL1, RELAY8.COIL1, RELAY6.COIL1, IN20.pin1, IN16.pin1, IN17.pin1, IN18.pin1, RELAY10.COIL2, RELAY7.COIL1, IN21.pin1, D3.anode, D4.anode, SW4.L1, SW4.COM, FUSE4.pin2
  N7: U1.D5, IN20.pin2
  N8: U1.D6, IN15.pin2
  N9: U1.D7, IN16.pin2
  N10: U1.D8, IN17.pin2
  N11: U1.RX, IN18.pin2
  N12: U1.TX, IN19.pin2
  N13: U1.Vin, IN21.pin2, D3.cathode, D4.cathode, SW4.L2, FUSE4.pin1
  N14: U1.S3, RELAY5.COIL2
  N15: OUT11.pin1, RELAY8.B
  N16: OUT11.pin2, RELAY8.C
  N17: OUT11.pin3, RELAY8.A
  N18: RELAY5.A, OUT10.pin3
  N19: RELAY5.C, OUT10.pin2
  N20: RELAY5.B, OUT10.pin1
  N21: RELAY6.A, OUT13.pin3
  N22: RELAY6.C, OUT13.pin2
  N23: RELAY6.B, OUT13.pin1
  N24: OUT12.pin1, RELAY7.B
  N25: OUT12.pin2, RELAY7.C
  N26: OUT12.pin3, RELAY7.A
  N27: RELAY9.A, OUT14.pin3
  N28: RELAY9.C, OUT14.pin2
  N29: RELAY9.B, OUT14.pin1
  N30: RELAY10.A, OUT15.pin3
  N31: RELAY10.C, OUT15.pin2
  N32: RELAY10.B, OUT15.pin1

notes:
  IN+
  IN-
  -
  +

custom parts:
  ESP8266 NodeMCU LoLin module: ESP8266 based NodeMCU
