# Fritzing sketch DP H01 (saved by Fritzing 0.9.3b)
circuit board: 10cm x 10cm
breadboards: 1

parts:
  NODEMCU = ESP8266 NodeMCU LoLin module
  IN2_D1 = screw terminal, 2 pins
  IN3_D2 = screw terminal, 2 pins
  IN4_D3 = screw terminal, 2 pins
  IN5_D5 = screw terminal, 2 pins
  IN6_TX = screw terminal, 2 pins
  IN1_D0 = screw terminal, 2 pins
  RELAY2 = OMRON PCB Power Relay – G5LE [part_number="G5LE-1\n" package=THT]
  RELAY3 = OMRON PCB Power Relay – G5LE [part_number="G5LE-1\n" package=THT]
  RELAY5 = OMRON PCB Power Relay – G5LE [part_number="G5LE-1\n" package=THT]
  RELAY4 = OMRON PCB Power Relay – G5LE [part_number="G5LE-1\n" package=THT]
  OUT1_S3 = screw terminal, 3 pins
  OUT3_D8 = screw terminal, 3 pins
  OUT4_D7 = screw terminal, 3 pins
  OUT2_RX = screw terminal, 3 pins
  RELAY6 = OMRON PCB Power Relay – G5LE [part_number="G5LE-1\n" package=THT]
  RELAY1 = OMRON PCB Power Relay – G5LE [part_number="G5LE-1\n" package=THT]
  OUT5_D6 = screw terminal, 3 pins
  OUT16 = screw terminal, 3 pins
  IN = screw terminal, 2 pins
  LM320 = Voltage Regulator [package=to220-adj]
  R11 = Resistor [tolerance=±5% resistance=220 package=THT]
  D5 = Rectifier Diode [part_number=1N4001 package="300 mil [THT]"]
  D6 = Rectifier Diode [part_number=1N4001 package="300 mil [THT]"]
  SW5 = Toggle Switch [package=THT]
  FUSE5 = female pin header, 2 pins [form="♀ (female)"]
  N2003 = ULN2003A [package="DIP16 [THT]"]
  LED1 = LED - 5mm [color="Red (633nm)" package="5 mm [THT]"]
  R13 = Resistor [tolerance=±5% resistance=220 package=THT]
  S1 = Toggle Switch [package=THT]
  LED2 = LED - 5mm [color="Red (633nm)" package="5 mm [THT]"]

nets:
  N1: NODEMCU.D0, IN1_D0.pin1
  N2: NODEMCU.D1, IN2_D1.pin1
  N3: NODEMCU.D2, IN3_D2.pin1
  N4: NODEMCU.D3, IN4_D3.pin1
  N5: NODEMCU.D4, S1.COM
  N6: NODEMCU.GND, IN2_D1.pin2, IN3_D2.pin2, IN4_D3.pin2, IN5_D5.pin2, IN6_TX.pin2, IN1_D0.pin2, LM320.ADJ, R11.Pin_1, N2003.0V, R13.Pin_1, S1.L2
  N7: NODEMCU.D5, IN5_D5.pin1
  N8: NODEMCU.D6, N2003.In_7
  N9: NODEMCU.D7, N2003.In_6
  N10: NODEMCU.D8, N2003.In_5
  N11: NODEMCU.RX, N2003.In_4
  N12: NODEMCU.TX, IN6_TX.pin1
  N13: NODEMCU.3V3, S1.L1
  N14: NODEMCU.Vin, RELAY2.COIL1, RELAY3.COIL1, RELAY5.COIL1, RELAY4.COIL1, RELAY6.COIL2, RELAY1.COIL1, LM320.OUT, N2003.COM_-_Common, LED1.anode, LED2.anode
  N15: NODEMCU.S2, N2003.In_2
  N16: NODEMCU.S3, N2003.In_3
  N17: RELAY2.A, OUT2_RX.pin3
  N18: RELAY2.C, OUT2_RX.pin2
  N19: RELAY2.COIL2, N2003.Out_4
  N20: RELAY2.B, OUT2_RX.pin1
  N21: RELAY3.A, OUT3_D8.pin3
  N22: RELAY3.C, OUT3_D8.pin2
  N23: RELAY3.COIL2, N2003.Out_5
  N24: RELAY3.B, OUT3_D8.pin1
  N25: RELAY5.A, OUT5_D6.pin3
  N26: RELAY5.C, OUT5_D6.pin2
  N27: RELAY5.COIL2, N2003.Out_7
  N28: RELAY5.B, OUT5_D6.pin1
  N29: RELAY4.A, OUT4_D7.pin3
  N30: RELAY4.C, OUT4_D7.pin2
  N31: RELAY4.COIL2, N2003.Out_6
  N32: RELAY4.B, OUT4_D7.pin1
  N33: OUT1_S3.pin1, RELAY1.B
  N34: OUT1_S3.pin2, RELAY1.C
  N35: OUT1_S3.pin3, RELAY1.A
  N36: RELAY6.A, OUT16.pin1
  N37: RELAY6.COIL1, N2003.Out_2, LED2.cathode
  N38: RELAY6.C, OUT16.pin2
  N39: RELAY6.B, OUT16.pin3
  N40: RELAY1.COIL2, N2003.Out_3
  N41: IN.pin1, FUSE5.pin1
  N42: IN.pin2, SW5.L1
  N43: LM320.IN, D5.cathode, D6.cathode, FUSE5.pin2
  N44: R11.Pin_0, D5.anode, D6.anode, SW5.COM, SW5.L2
  N45: LED1.cathode, R13.Pin_0

notes:
  IN+
  IN-
  -
  +
  MADE IN EGYPT
  DP COMPANY
  DP H01

custom parts:
  ESP8266 NodeMCU LoLin module: ESP8266 based NodeMCU
